# Fritzing sketch ESP12F D1 Biped Servo PCB (saved by Fritzing 0.9.3b)
circuit board: 2.57652cm x 3.45199cm
breadboards: 1

parts:
  WeMos_D1_Mini1 = WeMos D1 Mini
  M1 = Dagu DGServo 9g (Top view) [part_number=RS001B]
  M2 = Dagu DGServo 9g (Top view) [part_number=RS001B]
  M3 = Dagu DGServo 9g (Top view) [part_number=RS001B]
  M4 = Dagu DGServo 9g (Top view) [part_number=RS001B]
  M5 = Dagu DGServo 9g (Top view) [part_number=RS001B]
  M6 = Dagu DGServo 9g (Top view) [part_number=RS001B]
  M7 = Dagu DGServo 9g (Top view) [part_number=RS001B]
  M8 = Dagu DGServo 9g (Top view) [part_number=RS001B]
  M9 = Dagu DGServo 9g (Top view) [part_number=RS001B]
  BATT1 = 4xAA Switchable Battery Pack w/Bare Wire
  J1 = female pin header, 2 pins [form="♀ (female)"]
  C1 = Electrolytic Capacitor [capacitance=1µF package="100 mil [THT, electrolytic]"]
  C2 = Electrolytic Capacitor [capacitance=1µF package="100 mil [THT, electrolytic]"]
  J2 = female pin header, 2 pins [form="♀ (female)"]

nets:
  N1: WeMos_D1_Mini1.3V3, C1.+, C2.+
  VCC: WeMos_D1_Mini1.5V, M1.vcc, M2.vcc, M3.vcc, M4.vcc, M5.vcc, M6.vcc, M7.vcc, M8.vcc, M9.vcc, J1.pin1
  N2: WeMos_D1_Mini1.D0, M5.pulse
  N3: WeMos_D1_Mini1.D1, M1.pulse
  N4: WeMos_D1_Mini1.D2, M2.pulse
  N5: WeMos_D1_Mini1.D3, M3.pulse
  N6: WeMos_D1_Mini1.D4, M9.pulse
  N7: WeMos_D1_Mini1.D5, M6.pulse
  N8: WeMos_D1_Mini1.D6, M7.pulse
  N9: WeMos_D1_Mini1.D7, M8.pulse
  N10: WeMos_D1_Mini1.D8, M4.pulse
  GND: WeMos_D1_Mini1.G, M1.gnd, M2.gnd, M3.gnd, M4.gnd, M5.gnd, M6.gnd, M7.gnd, M8.gnd, M9.gnd, BATT1.NEG, C1.-, C2.-, J2.pin1
  N11: BATT1.POS, J1.pin2, J2.pin2

custom parts:
  4xAA Switchable Battery Pack w/Bare Wire: 4xAA Switchable Battery Pack with Bare Wire connection
